// Logisim project circuito_cpu.circ as structural Verilog
module main (
);

  wire alu_br, alu_src, br, branch_en_out, clk, mem_r, mem_reg, mem_w, pc_reg_alu, pc_reg_br,
       subctrlsys_reg_write;
  wire [2:0] alu_op;
  wire [3:0] alu_ctrl_sys_opcode;
  wire [23:0] alu_block_out_r;
  wire [31:0] immediate_gen_imm, multiplexer_1_out, multiplexer_2_out, multiplexer_3_out, pc,
       program_mem_data, register_file_reg_a_data, register_file_reg_b_data;
  wire [31:24] alu_block_out_r_2;

  and branch_en (branch_en_out, alu_br, br);
  prog_count u_pc (
    .clk(clk), .imm(immediate_gen_imm), .branch(branch_en_out), .pc_reg_mux(pc_reg_br),
    .reg_in(register_file_reg_a_data), .pc(pc));
  ROM #(.addrWidth(24), .dataWidth(32), .misaligned("true")) program_mem (.addr(pc[23:0]), .data(program_mem_data));
  Clock clk_src (.out(clk));
  ctrl_unit subctrlsys (
    .instr(program_mem_data), .pc_reg(pc_reg_alu), .alu_op(alu_op), .branch(br), .mem_read(mem_r),
    .mem_write(mem_w), .mem_to_reg(mem_reg), .alu_src(alu_src), .reg_write(subctrlsys_reg_write),
    .pc_reg_branch(pc_reg_br));
  reg_file register_file (
    .clk(clk), .write_en(subctrlsys_reg_write), .write_data(multiplexer_3_out),
    .write_addr(program_mem_data[11:7]), .reg_a_addr(program_mem_data[19:15]),
    .reg_b_addr(program_mem_data[24:20]), .reg_a_data(register_file_reg_a_data),
    .reg_b_data(register_file_reg_b_data));
  imm_gen immediate_gen (.instr(program_mem_data), .imm(immediate_gen_imm));
  Multiplexer #(.enable("false"), .width(32)) multiplexer_1 (
    .in0(register_file_reg_a_data), .in1(pc), .out(multiplexer_1_out), .sel(pc_reg_alu));
  Multiplexer #(.enable("false"), .width(32)) multiplexer_2 (
    .in0(register_file_reg_b_data), .in1(immediate_gen_imm), .out(multiplexer_2_out), .sel(alu_src));
  alu_ctrl alu_ctrl_sys (.alu_op(alu_op), .instruction(program_mem_data), .opcode(alu_ctrl_sys_opcode));
  alu alu_block (
    .in_a(multiplexer_1_out), .in_b(multiplexer_2_out), .op(alu_ctrl_sys_opcode),
    .out_r({alu_block_out_r_2, alu_block_out_r}), .aux_br(alu_br));
  RAM #(.addrWidth(24), .dataWidth(32), .databus("bidir"), .enables("line"), .trigger("falling")) data_mem (
    .addr(alu_block_out_r), .we(mem_w), .oe(mem_r), .clk(clk), .data(register_file_reg_b_data));
  Multiplexer #(.enable("false"), .width(32)) multiplexer_3 (
    .in0({alu_block_out_r_2, alu_block_out_r}), .in1(register_file_reg_b_data), .out(multiplexer_3_out),
    .sel(mem_reg));

  // Notes on the sheet:
  //   contents of program_mem (hex, n*v repeats v):
  //   8c00113 1823 8c00113 1823 1823 1823 100000 100011
endmodule

// VHDL entity prog_count, as the project stores it:
library ieee;
use ieee.std_logic_1164.all;
use ieee.numeric_std.all;

entity prog_count is
    port(
        clk : in std_logic;
        imm : in std_logic_vector(31 downto 0);
        branch : in std_logic;
        pc_reg_mux : in std_logic;
        reg_in : in std_logic_vector(31 downto 0);
        pc : out std_logic_vector(31 downto 0)
    );
end prog_count;

architecture Behavioral of prog_count is
    signal immediate, ptr_pc : std_logic_vector(31 downto 0) := (others => '0');
    signal addr_sum : std_logic_vector(31 downto 0) := (others => '0');
    begin 
    	   addr_sum(0) <= '1';
        immediate <= imm;
        pc <= ptr_pc;

        fetch_instr: process(clk, ptr_pc, branch, pc_reg_mux) is
        begin
            if rising_edge(clk) then
                if branch = '1' then
                	if pc_reg_mux = '1' then
                    	ptr_pc <= std_logic_vector(unsigned(ptr_pc) + unsigned(immediate));
                    else
                    	ptr_pc <= std_logic_vector(unsigned(reg_in) + unsigned(immediate));
                    end if;
                else
                    ptr_pc <= std_logic_vector(unsigned(ptr_pc) + unsigned(addr_sum));
                end if;
            end if;
        end process fetch_instr;
end Behavioral;

// VHDL entity reg_file, as the project stores it:
library ieee;
use ieee.std_logic_1164.all;
use ieee.numeric_std.all;

entity reg_file is
    port(
        clk : in std_logic;
        write_en : in std_logic;

        write_data : in std_logic_vector(31 downto 0);
        
        write_addr : in std_logic_vector(4 downto 0);
        reg_a_addr : in std_logic_vector(4 downto 0);
        reg_b_addr : in std_logic_vector(4 downto 0);

        reg_a_data : out std_logic_vector(31 downto 0);
        reg_b_data : out std_logic_vector(31 downto 0)
    );
end reg_file;

architecture Behavioral of reg_file is
    -- 32 registradores de 32 bits
    type register_mem is array (integer range <>) of std_logic_vector(31 downto 0);
    signal register_bank : register_mem(0 to 31) := (others => x"00000000");

    begin
        reg_a_data <= register_bank(to_integer(unsigned(reg_a_addr)));
        reg_b_data <= register_bank(to_integer(unsigned(reg_b_addr)));
        
        register_access: process(clk, write_en, write_addr) is
        begin
            -- na borda de subida
            if rising_edge(clk) and write_en = '1' then
            	register_bank(to_integer(unsigned(write_addr))) <= write_data;
            end if;
        end process register_access;

end Behavioral;

// VHDL entity imm_gen, as the project stores it:
library ieee;
use ieee.std_logic_1164.all;
use ieee.numeric_std.all;

entity imm_gen is
    port(
        instr : in std_logic_vector(31 downto 0);
        imm : out std_logic_vector(31 downto 0)
    );
end imm_gen;

architecture Behavioral of imm_gen is
begin
    decode_instr : process(instr)
    begin
        -- logica para fazer decode da instrução
        case instr(6 downto 0) is
            when "0110111" => -- lui
                imm(31 downto 12) <= instr(31 downto 12);
                imm(11 downto 0) <= (others => '0');
            when "0010111" => -- auipc
                imm(31 downto 12) <= instr(31 downto 12);
                imm(11 downto 0) <= (others => '0');
            when "1101111" => -- jal
                imm(0) <= '0';
                imm(20 downto 1) <= instr(31) & instr(19 downto 12) & instr(20) & instr(30 downto 21);
                imm(31 downto 21) <= (others => instr(31));
            when "1100111" => -- jalr
                imm(11 downto 0) <= instr(31 downto 20);
                imm(31 downto 12) <= (others => instr(31));
            when "1100011" => -- branch
                imm(0) <= '0';
                imm(12 downto 1) <= instr(31) & instr(7) & instr(30 downto 25) & instr(11 downto 8);
                imm(31 downto 13) <= (others => instr(31));
            when "0000011" => -- load
                imm(11 downto 0) <= instr(31 downto 20);
                imm(31 downto 12) <= (others => instr(31));
            when "0100011" => -- store
                imm(11 downto 0) <= instr(31 downto 25) & instr(11 downto 7);
                imm(31 downto 12) <= (others => instr(31));
            when "0010011" => -- i-type
                if (instr(13) or (not instr(12))) = '1' then -- andi, ori, xori, 
                    imm(11 downto 0) <= instr(31 downto 20);
                    imm(31 downto 12) <= (others => instr(31));
                else                               -- slli e srli
                    imm(4 downto 0) <= instr(24 downto 20);
                    imm(31 downto 5) <= (others => instr(31));
                end if;
            when others => -- outros
                imm <= (others => 'X');
        end case;
    end process decode_instr;
end architecture;

// VHDL entity ctrl_unit, as the project stores it:
library ieee;
use ieee.std_logic_1164.all;


entity ctrl_unit is
    port(
        instr : in std_logic_vector(31 downto 0);
        pc_reg : out std_logic; -- 0 -> pc, 1 -> reg1
        alu_op : out std_logic_vector(2 downto 0); -- alu opcode
        branch : out std_logic; -- 0 -> não é branch e 1 -> é branch
        mem_read : out std_logic; -- 0 -> sem leitura, 1 -> leitura
        mem_write : out std_logic; -- 0 -> sem escrita, 1 -> escrita
        mem_to_reg : out std_logic; -- 0 -> alu, 1 -> mem
        alu_src : out std_logic; -- 0 -> reg, 1 -> imediato
        reg_write : out std_logic; -- 0 -> leitura , 1 -> escrita
        pc_reg_branch : out std_logic -- 0 -> pc, 1 -> reg1 (mux de entrada do somador do branch)
    );
end ctrl_unit;

architecture Behavioral of ctrl_unit is
begin
    -- alu_op           operação
    --  000     nop
    --  001     logico-aritmética (R-type)
    --  010     logico-aritmética (I-type)
    --  011     branch (equal or not equal)
    --  100     adição in1 + in2
    --  101     adição in1 + 4
    --  110     passa o imediato (in2) direto pra saída
    --  111     nop

    ctrl_decode : process(instr)
    begin
        case instr(6 downto 0) is
            when "0110011" => -- instruções tipo R
                reg_write <= '1'; -- escreve no reg
                mem_to_reg <= '0'; -- passa alu
                mem_write <= 'X';  -- não é mem
                mem_read <= 'X'; 
                branch <= '0'; -- sem branch
                alu_src <= '0'; -- reg
                alu_op <= "001"; -- (logico-aritmética)
                pc_reg <= '0'; -- passa reg
                pc_reg_branch <= '0'; -- passa pc
            when "0010011" => -- instruções tipo I
                reg_write <= '1';
                mem_to_reg <= '0'; -- passa alu
                mem_write <= 'X';  -- não é mem
                mem_read <= 'X'; 
                branch <= '0'; -- sem branch
                alu_src <= '1'; -- imediato
                alu_op <= "010"; -- (logico-aritmética)
                pc_reg <= '0'; -- passa reg
                pc_reg_branch <= '0'; -- passa pc
            when "1100011" => -- instruções de branch
                reg_write <= '0';
                mem_to_reg <= 'X'; -- não escreve em reg
                mem_write <= 'X';  -- não é mem
                mem_read <= 'X';
                branch <= '1'; -- branch
                alu_src <= '0'; -- reg
                alu_op <= "011"; -- (equal or not equal)
                pc_reg <= '0'; -- passa reg
                pc_reg_branch <= '0'; -- passa pc
            when "0010111" => -- auipc
                reg_write <= '1';
                mem_to_reg <= '0'; -- passa alu
                mem_write <= 'X';  -- não é mem
                mem_read <= 'X';
                branch <= '0'; -- sem branch
                alu_src <= '1'; -- imediato
                alu_op <= "100"; -- (add)
                pc_reg <= '1'; -- pc
                pc_reg_branch <= '0'; -- passa pc
            when "0110111" => -- lui
                reg_write <= '1';
                mem_to_reg <= '0'; -- passa alu
                mem_write <= 'X';  -- não é mem
                mem_read <= 'X';
                branch <= '0'; -- sem branch
                alu_src <= '1'; -- imediato
                alu_op <= "110"; -- (passa o imediato pra saída da ALU)
                pc_reg <= 'X'; -- essa entrada não é processada nessa alu_op
                pc_reg_branch <= '0'; -- passa pc
            when "0000011" => -- lw
                reg_write <= '1';
                mem_to_reg <= '1'; -- passa mem
                mem_write <= '0';  -- le na memória
                mem_read <= '1';
                branch <= '0'; -- sem branch
                alu_src <= '1'; -- imediato
                alu_op <= "100"; -- (add)
                pc_reg <= '0'; -- passa reg
                pc_reg_branch <= '0'; -- passa pc
            when "0100011" => -- sw
                reg_write <= '0';
                mem_to_reg <= 'X'; -- não escreve em reg
                mem_write <= '1';  -- escreve na memória
                mem_read <= '0';
                branch <= '0'; -- sem branch
                alu_src <= '1'; -- imediato
                alu_op <= "100"; -- (add)
                pc_reg <= '0'; -- passa reg
                pc_reg_branch <= '0'; -- passa pc
            when "1101111" => -- jal
                reg_write <= '1';
                mem_to_reg <= '0'; -- passa alu
                mem_write <= 'X';  -- não é mem
                mem_read <= 'X';
                branch <= '1'; -- branch
                alu_src <= '1'; -- imediato
                alu_op <= "101"; --(add + 4)
                pc_reg <= '1'; -- passa pc
                pc_reg_branch <= '0'; -- passa pc
            when "1100111" => -- jalr
                reg_write <= '1';
                mem_to_reg <= '0'; -- passa alu
                mem_write <= 'X';  -- não é mem
                mem_read <= 'X';
                branch <= '1'; -- branch
                alu_src <= '1'; -- imediato
                alu_op <= "101"; --(add + 4)
                pc_reg <= '1'; -- passa pc
                pc_reg_branch <= '1'; -- passa reg1
            when others =>
                reg_write <= 'X';
                mem_to_reg <= 'X';
                mem_write <= 'X'; 
                mem_read <= 'X';
                branch <= 'X'; 
                alu_src <= 'X'; 
                alu_op <= "XXX";
                pc_reg <= 'X'; 
                pc_reg_branch <= 'X';
        end case;
    end process ctrl_decode;
end architecture;

// VHDL entity alu, as the project stores it:
library ieee;
use ieee.std_logic_1164.all;
use ieee.numeric_std.all;

entity alu is
    port(
        in_a, in_b : in std_logic_vector(31 downto 0);
        op : in std_logic_vector(3 downto 0);
        out_r : out std_logic_vector(31 downto 0);
        aux_br : out std_logic
    );
end alu;

-- Operação  OPCODE  Br_aux
-- nop        0000     0
-- Soma       0001     0 
-- Sub        0010     0
-- and        0011     0
-- or         0100     0
-- xor        0101     0
-- sll        0110     0
-- srl        0111     0
-- equal      1000     1 if equal
-- ~equal     1001     1 if not equal
-- in1 + 1    1010     1
-- out = in2  1011     0
-- nop        others   0
architecture Behavioral of alu is
    begin

    process(in_a, in_b, op)
    begin
        case op is
            when "0001" => 
                out_r <= std_logic_vector(unsigned(in_a) + unsigned(in_b));
                aux_br <= '0';
            when "0010" => 
                out_r <= std_logic_vector(unsigned(in_a) - unsigned(in_b));
                aux_br <= '0';
            when "0011" => 
                out_r <= in_a and in_b;
                aux_br <= '0';
            when "0100" =>
                out_r <= in_a or in_b;
            when "0101" => 
                out_r <= in_a xor in_b;
                aux_br <= '0';
            when "0110" => 
                out_r <= std_logic_vector(shift_left(unsigned(in_a), to_integer(unsigned(in_b(4 downto 0)))));
                aux_br <= '0';
            when "0111" => 
                out_r <= std_logic_vector(shift_right(unsigned(in_a), to_integer(unsigned(in_b(4 downto 0)))));
                aux_br <= '0';
            when "1000" => 
                out_r <= (others => 'X');
                if in_a = in_b then
                	aux_br <= '1';
                else aux_br <= '0';
                end if;
            when "1001" => 
                out_r <= (others => 'X');
                if in_a /= in_b then
                	aux_br <= '1';
                else aux_br <= '0';
                end if;
            when "1010" => 
                out_r <= std_logic_vector(unsigned(in_a) + 1);
                aux_br <= '1';
            when "1011" => 
                out_r <= in_b;
                aux_br <= '0';
            when others => 
                out_r <= in_a;
                aux_br <= '0';
        end case;
    end process;
end Behavioral;

// VHDL entity alu_ctrl, as the project stores it:
library ieee;
use ieee.std_logic_1164.all;

entity alu_ctrl is
    port(
        alu_op: in std_logic_vector(2 downto 0);
        instruction: in std_logic_vector(31 downto 0);
        opcode: out std_logic_vector(3 downto 0)
    );
end alu_ctrl;

-- Operação  OPCODE  Br_aux
-- nop        0000     0
-- Soma       0001     0 
-- Sub        0010     0
-- and        0011     0
-- or         0100     0
-- xor        0101     0
-- sll        0110     0
-- srl        0111     0
-- equal      1000     1 if equal
-- ~equal     1001     1 if not equal
-- in1 + 1    1010     1
-- out = in2  1011     0
-- nop        others   0

architecture Behavioral of alu_ctrl is
    signal funct3 : std_logic_vector(2 downto 0) := (others => '0');
    signal funct7 : std_logic_vector(6 downto 0) := (others => '0');

begin

    funct3 <= instruction(14 downto 12);
    funct7 <= instruction(31 downto 25);

    op_decode: process(alu_op, funct3, funct7) is
        begin
            if alu_op = "001" or alu_op = "010" then
                if funct3 = "000" and alu_op = "001" then
	                if funct7 = "0000000" then -- add
	                    opcode <= "0001";
	                elsif funct7 = "0100000" then -- sub
	                    opcode <= "0010";
	                end if;
	           elsif funct3 = "000" and alu_op = "010" then
	           	opcode <= "0001";
	           elsif funct3 = "001" then -- sll
	                opcode <= "0110";
	           elsif funct3 = "100" then -- xor
	                opcode <= "0101";
	           elsif funct3 = "101" then -- srl
	                opcode <= "0111";
	           elsif funct3 = "110" then -- or
	                opcode <= "0100";
	           elsif funct3 = "111" then -- and
	                opcode <= "0011";
	           end if;
            elsif alu_op = "011" then
                if funct3 = "000" then -- beq
                    opcode <= "1000";
                elsif funct3 = "001" then -- bne
                    opcode <= "1001";
                end if;
            elsif alu_op = "100" then
                opcode <= "0001";
            elsif alu_op = "101" then
                opcode <= "1010";
            elsif alu_op = "110" then
                opcode <= "1011";
            elsif alu_op = "111" or alu_op = "000" then
                opcode <= "0000";
            end if;
    end process op_decode;

end Behavioral;
